// Logisim project logisimproj.circ as structural Verilog: 1 circuit, main circuit main
module main (
);

  wire and_1_out, and_2_out, and_3_out, and_4_out, clock_1_out, counter_2_carry, counter_3_carry,
       counter_4_carry, counter_5_carry;
  wire [1:0] bcd_to_7_segment_decoder_1_p1;
  wire [2:0] counter_3_q;
  wire [3:0] bcd_to_7_segment_decoder_2_p1, counter_4_q;

  _7_Segment_Display u_7_segment_display_1 (.dp(clock_1_out));  // open: g, f, a, b, e, d, c
  and and_1 (and_1_out, bcd_to_7_segment_decoder_1_p1[1], bcd_to_7_segment_decoder_2_p1[2]);
  Clock clock_1 (.out(clock_1_out));
  _7_Segment_Display u_7_segment_display_2 ();  // open: g, f, a, b, e, d, c, dp
  // BCD_to_7_Segment_decoder bcd_to_7_segment_decoder_1: pin names not known; wires that end beside it: {2'b00, bcd_to_7_segment_decoder_1_p1}
  Counter #(.max('h2), .width(2)) counter_1 (
    .count(and_2_out), .Q(bcd_to_7_segment_decoder_1_p1), .clk(clock_1_out), .clr(and_1_out));  // open: load, D, carry, up
  and and_2 (and_2_out, counter_5_carry, counter_4_carry, counter_2_carry, counter_3_carry);
  _7_Segment_Display u_7_segment_display_3 ();  // open: g, f, a, b, e, d, c, dp
  // BCD_to_7_Segment_decoder bcd_to_7_segment_decoder_2: pin names not known; wires that end beside it: bcd_to_7_segment_decoder_2_p1
  Counter #(.max('h9), .width(4)) counter_2 (
    .count(and_3_out), .Q(bcd_to_7_segment_decoder_2_p1), .carry(counter_2_carry), .clk(clock_1_out),
    .clr(and_1_out));  // open: load, D, up
  Counter #(.max('h5), .width(3)) counter_3 (
    .count(and_4_out), .Q(counter_3_q), .carry(counter_3_carry), .clk(clock_1_out), .clr(and_1_out));  // open: load, D, up
  _7_Segment_Display u_7_segment_display_4 ();  // open: g, f, a, b, e, d, c, dp
  // BCD_to_7_Segment_decoder bcd_to_7_segment_decoder_3: pin names not known; wires that end beside it: {1'b0, counter_3_q}
  Counter #(.max('h9), .width(4)) counter_4 (
    .count(counter_5_carry), .Q(counter_4_q), .carry(counter_4_carry), .clk(clock_1_out), .clr(and_1_out));  // open: load, D, up
  and and_3 (and_3_out, counter_3_carry, and_4_out, counter_4_carry);
  _7_Segment_Display u_7_segment_display_5 ();  // open: g, f, a, b, e, d, c, dp
  // BCD_to_7_Segment_decoder bcd_to_7_segment_decoder_4: pin names not known; wires that end beside it: counter_4_q
  Counter #(.max('h3b), .width(6)) counter_5 (
    .carry(counter_5_carry), .clk(clock_1_out), .clr(and_1_out));  // open: load, D, count, Q, up
  and and_4 (and_4_out, counter_4_carry, counter_5_carry);
endmodule
